// Logisim project dds-proj.circ as structural Verilog: 6 circuits, main circuit main
module main (
  input  [3:0] Request_floor_input
);

  wire clock_out, demultiplexer_1_out1, demultiplexer_1_out2, Lift_1_controller_lift_im,
       lift_controller_1_lift_im, n7seg_decoder_1_a_2, n7seg_decoder_1_b_2, n7seg_decoder_1_c_2,
       n7seg_decoder_1_d_2, n7seg_decoder_1_e, n7seg_decoder_1_f, n7seg_decoder_1_g, n7seg_decoder_2_a_2,
       n7seg_decoder_2_b_2, n7seg_decoder_2_c_2, n7seg_decoder_2_d_2, n7seg_decoder_2_e, n7seg_decoder_2_f,
       n7seg_decoder_2_g, n7seg_decoder_3_a_2, n7seg_decoder_3_b_2, n7seg_decoder_3_c_2, n7seg_decoder_3_d_2,
       n7seg_decoder_3_e, n7seg_decoder_3_f, n7seg_decoder_3_g, Reset_out;
  wire [1:0] logic_circuit_chosen_lift, selected_lift_q;
  wire [3:0] Lift_1_controller_lift_floor, Lift_1_controller_lift_md, lift_controller_1_lift_floor,
       lift_controller_1_lift_md;

  Button Reset (.out(Reset_out));
  Clock clock (.out(clock_out));
  _7seg_decoder u_7seg_decoder_1 (
    .D(Request_floor_input[0]), .C(Request_floor_input[1]), .B(Request_floor_input[2]),
    .A(Request_floor_input[3]), .a_2(n7seg_decoder_1_a_2), .b_2(n7seg_decoder_1_b_2),
    .c_2(n7seg_decoder_1_c_2), .d_2(n7seg_decoder_1_d_2), .e(n7seg_decoder_1_e), .f(n7seg_decoder_1_f),
    .g(n7seg_decoder_1_g));
  lift_controller Lift_1_controller (
    .req_floor(Request_floor_input), .selector(demultiplexer_1_out1), .clock(clock_out), .Reset(Reset_out),
    .lift_im(Lift_1_controller_lift_im), .lift_floor(Lift_1_controller_lift_floor),
    .lift_md(Lift_1_controller_lift_md));
  lift_controller lift_controller_1 (
    .req_floor(Request_floor_input), .selector(demultiplexer_1_out2), .clock(clock_out), .Reset(Reset_out),
    .lift_im(lift_controller_1_lift_im), .lift_floor(lift_controller_1_lift_floor),
    .lift_md(lift_controller_1_lift_md));
  _7_Segment_Display u_7_segment_display_1 (
    .g(n7seg_decoder_1_g), .f(n7seg_decoder_1_f), .a(n7seg_decoder_1_a_2), .b(n7seg_decoder_1_b_2),
    .e(n7seg_decoder_1_e), .d(n7seg_decoder_1_d_2), .c(n7seg_decoder_1_c_2));  // open: dp
  _7seg_decoder u_7seg_decoder_2 (
    .D(Lift_1_controller_lift_floor[0]), .C(Lift_1_controller_lift_floor[1]),
    .B(Lift_1_controller_lift_floor[2]), .A(Lift_1_controller_lift_floor[3]), .a_2(n7seg_decoder_2_a_2),
    .b_2(n7seg_decoder_2_b_2), .c_2(n7seg_decoder_2_c_2), .d_2(n7seg_decoder_2_d_2), .e(n7seg_decoder_2_e),
    .f(n7seg_decoder_2_f), .g(n7seg_decoder_2_g));
  _7_Segment_Display u_7_segment_display_2 (
    .g(n7seg_decoder_2_g), .f(n7seg_decoder_2_f), .a(n7seg_decoder_2_a_2), .b(n7seg_decoder_2_b_2),
    .e(n7seg_decoder_2_e), .d(n7seg_decoder_2_d_2), .c(n7seg_decoder_2_c_2));  // open: dp
  Register #(.width(2)) selected_lift (
    .D(logic_circuit_chosen_lift), .Q(selected_lift_q), .clk(clock_out));  // open: en, clr
  Demultiplexer #(.select(2), .enable("false")) demultiplexer_1 (
    .out1(demultiplexer_1_out1), .out2(demultiplexer_1_out2), .in(1'b1), .sel(selected_lift_q));  // open: out0, out3
  \logic  logic_circuit (
    .lift_1_im(Lift_1_controller_lift_im), .lift_2_im(lift_controller_1_lift_im),
    .floor_1(Lift_1_controller_lift_floor), .floor_2(lift_controller_1_lift_floor),
    .req_floor(Request_floor_input), .lift_1_md(Lift_1_controller_lift_md),
    .lift_2_md(lift_controller_1_lift_md), .chosen_lift(logic_circuit_chosen_lift));
  _7seg_decoder u_7seg_decoder_3 (
    .D(lift_controller_1_lift_floor[0]), .C(lift_controller_1_lift_floor[1]),
    .B(lift_controller_1_lift_floor[2]), .A(lift_controller_1_lift_floor[3]), .a_2(n7seg_decoder_3_a_2),
    .b_2(n7seg_decoder_3_b_2), .c_2(n7seg_decoder_3_c_2), .d_2(n7seg_decoder_3_d_2), .e(n7seg_decoder_3_e),
    .f(n7seg_decoder_3_f), .g(n7seg_decoder_3_g));
  _7_Segment_Display u_7_segment_display_3 (
    .g(n7seg_decoder_3_g), .f(n7seg_decoder_3_f), .a(n7seg_decoder_3_a_2), .b(n7seg_decoder_3_b_2),
    .e(n7seg_decoder_3_e), .d(n7seg_decoder_3_d_2), .c(n7seg_decoder_3_c_2));  // open: dp

  // Notes on the sheet:
  //   Lift 2 controller
  //   Request floor
  //   Smart elevator controller
  //   Lift 1 floor
  //   To use, enter input at "Request floor input", then start the simulation
  //   -The circuit will then decide which elevator to move and move it accordingly in real time
  //   There are two displays which currently show which floor each elevator is on
  //   Lift 2 floor
endmodule

module new_reg (
  input  [3:0] req_floor,
  input  [1:0] lift_choice
);

  wire and_1_out, clock_1_out, comparator_1_eq, comparator_1_gt, comparator_2_eq, comparator_2_gt,
       comparator_2_lt, demultiplexer_1_out1, is_moving_q, not_1_out, or_1_out, or_2_out, or_3_out,
       xnor_1_out;
  wire [1:0] register_1_q;
  wire [3:0] cur_floor_q, max_d_q;

  or or_1 (or_1_out, demultiplexer_1_out1, not_1_out);
  and and_1 (and_1_out, demultiplexer_1_out1, xnor_1_out);
  Clock clock_1 (.out(clock_1_out));
  Register #(.width(1), .trigger("falling")) is_moving (
    .D(or_1_out), .Q(is_moving_q), .clk(clock_1_out));  // open: en, clr
  Register #(.width(4)) max_d (.D(req_floor), .Q(max_d_q), .clk(and_1_out));  // open: en, clr
  Counter #(.width(4), .max('hf)) cur_floor (
    .load(comparator_2_lt), .D(cur_floor_q), .count(is_moving_q), .Q(cur_floor_q), .clk(clock_1_out));  // open: carry, clr
  not not_1 (not_1_out, comparator_2_eq);
  Comparator #(.width(4)) comparator_1 (
    .a(req_floor), .b(max_d_q), .gt(comparator_1_gt), .eq(comparator_1_eq));  // open: lt
  Comparator #(.width(4)) comparator_2 (
    .a(max_d_q), .b(cur_floor_q), .gt(comparator_2_gt), .eq(comparator_2_eq), .lt(comparator_2_lt));
  or or_2 (or_2_out, comparator_1_gt, comparator_1_eq);
  or or_3 (or_3_out, comparator_2_gt, comparator_2_eq);
  xnor xnor_1 (xnor_1_out, or_2_out, or_3_out);
  Register #(.width(2)) register_1 (.D(lift_choice), .Q(register_1_q), .clk(clock_1_out));  // open: en, clr
  Demultiplexer #(.select(2), .enable("false")) demultiplexer_1 (
    .out1(demultiplexer_1_out1), .in(1'b1), .sel(register_1_q));  // open: out0, out2, out3
endmodule

module good_looking_stuff (
  input  [3:0] req_floor,
  input  [1:0] lift_choice
);

  wire and_1_out, clock_1_out, comparator_1_eq, comparator_1_gt, comparator_2_eq, comparator_2_gt,
       comparator_2_lt, demultiplexer_1_out1, demultiplexer_1_out2, is_moving_1_q, not_1_out, or_1_out,
       or_2_out, or_3_out, xnor_1_out;
  wire [1:0] register_1_q;
  wire [3:0] floor_1_q, max_d_1_q;

  or or_1 (or_1_out, not_1_out, demultiplexer_1_out1);
  Register #(.width(1), .trigger("falling")) is_moving_1 (
    .D(or_1_out), .Q(is_moving_1_q), .clk(clock_1_out));  // open: en, clr
  and and_1 (and_1_out, xnor_1_out, demultiplexer_1_out1);
  Register #(.width(4)) max_d_1 (.D(req_floor), .Q(max_d_1_q), .clk(and_1_out));  // open: en, clr
  Counter #(.width(4), .max('hf)) floor_1 (
    .load(comparator_2_lt), .D(floor_1_q), .count(is_moving_1_q), .Q(floor_1_q), .clk(clock_1_out));  // open: carry, clr
  not not_1 (not_1_out, comparator_2_eq);
  Comparator #(.width(4)) comparator_1 (
    .a(req_floor), .b(max_d_1_q), .gt(comparator_1_gt), .eq(comparator_1_eq));  // open: lt
  Comparator #(.width(4)) comparator_2 (
    .a(max_d_1_q), .b(floor_1_q), .gt(comparator_2_gt), .eq(comparator_2_eq), .lt(comparator_2_lt));
  or or_2 (or_2_out, comparator_1_gt, comparator_1_eq);
  or or_3 (or_3_out, comparator_2_gt, comparator_2_eq);
  xnor xnor_1 (xnor_1_out, or_2_out, or_3_out);
  Register #(.width(2)) register_1 (.D(lift_choice), .Q(register_1_q), .clk(clock_1_out));  // open: en, clr
  Demultiplexer #(.select(2), .enable("false")) demultiplexer_1 (
    .out1(demultiplexer_1_out1), .out2(demultiplexer_1_out2), .in(1'b1), .sel(register_1_q));  // open: out0, out3
  Clock clock_1 (.out(clock_1_out));
endmodule

module _7seg_decoder (
  input  D,
  input  C,
  input  B,
  input  A,
  output a_2,
  output b_2,
  output c_2,
  output d_2,
  output e,
  output f,
  output g
);

  wire and_1_out, and_2_out, and_3_out, and_4_out, and_5_out, and_6_out, and_7_out, and_8_out, and_9_out,
       and_10_out, and_11_out, and_12_out, and_13_out, and_14_out, and_15_out, and_16_out, not_1_out,
       not_2_out, not_3_out, not_4_out, not_5_out, not_6_out, not_7_out, not_8_out, not_9_out, not_10_out,
       not_11_out, not_12_out, not_13_out, not_14_out, not_15_out, not_16_out, not_17_out, not_18_out,
       not_19_out, not_20_out, not_21_out;

  not not_1 (not_1_out, D);
  and and_1 (and_1_out, not_1_out, not_2_out);
  not not_2 (not_2_out, B);
  and and_2 (and_2_out, D, B);
  not not_3 (not_3_out, D);
  and and_3 (and_3_out, not_3_out, not_4_out);
  not not_4 (not_4_out, C);
  not not_5 (not_5_out, B);
  and and_4 (and_4_out, D, C);
  not not_6 (not_6_out, C);
  or or_1 (c_2, not_6_out, B, D);
  not not_7 (not_7_out, D);
  and and_5 (and_5_out, not_7_out, not_8_out);
  not not_8 (not_8_out, B);
  not not_9 (not_9_out, D);
  and and_6 (and_6_out, not_9_out, C);
  and and_7 (and_7_out, C, not_10_out);
  not not_10 (not_10_out, B);
  and and_8 (and_8_out, D, not_11_out, B);
  not not_11 (not_11_out, C);
  not not_12 (not_12_out, D);
  and and_9 (and_9_out, not_12_out, not_13_out);
  not not_13 (not_13_out, B);
  not not_14 (not_14_out, D);
  and and_10 (and_10_out, not_14_out, C);
  not not_15 (not_15_out, D);
  and and_11 (and_11_out, not_15_out, not_16_out);
  not not_16 (not_16_out, C);
  not not_17 (not_17_out, D);
  and and_12 (and_12_out, not_17_out, B);
  not not_18 (not_18_out, C);
  and and_13 (and_13_out, not_18_out, B);
  not not_19 (not_19_out, C);
  and and_14 (and_14_out, not_19_out, B);
  not not_20 (not_20_out, D);
  and and_15 (and_15_out, not_20_out, C);
  and and_16 (and_16_out, C, not_21_out);
  not not_21 (not_21_out, B);
  or or_2 (a_2, and_1_out, A, C, and_2_out);
  or or_3 (b_2, and_3_out, not_5_out, and_4_out);
  or or_4 (d_2, and_5_out, A, and_6_out, and_7_out, and_8_out);
  or or_5 (e, and_9_out, and_10_out);
  or or_6 (f, and_11_out, A, and_12_out, and_13_out);
  or or_7 (g, A, and_14_out, and_15_out, and_16_out);
endmodule

module \logic  (
  input  lift_1_im,
  input  lift_2_im,
  input  [3:0] floor_1,
  input  [3:0] floor_2,
  input  [3:0] req_floor,
  input  [3:0] lift_1_md,
  input  [3:0] lift_2_md,
  output [1:0] chosen_lift
);

  wire and_1_out, comparator_1_gt, comparator_2_gt, comparator_3_gt, comparator_4_gt, comparator_5_gt,
       comparator_6_gt, comparator_7_gt, xnor_1_out, xnor_2_out;
  wire [1:0] multiplexer_1_out, multiplexer_2_out, multiplexer_5_out, multiplexer_6_out, multiplexer_7_out,
       multiplexer_8_out;
  wire [3:0] multiplexer_3_out, multiplexer_4_out, subtractor_1_out, subtractor_2_out, subtractor_3_out,
       subtractor_4_out;

  Comparator #(.width(4)) comparator_1 (.a(req_floor), .b(floor_1), .gt(comparator_1_gt));  // open: eq, lt
  Comparator #(.width(4)) comparator_2 (.a(lift_2_md), .b(floor_1), .gt(comparator_2_gt));  // open: eq, lt
  Comparator #(.width(4)) comparator_3 (.a(req_floor), .b(floor_2), .gt(comparator_3_gt));  // open: eq, lt
  Comparator #(.width(4)) comparator_4 (.a(lift_1_md), .b(floor_2), .gt(comparator_4_gt));  // open: eq, lt
  Comparator #(.width(4)) comparator_5 (.a(lift_1_md), .b(req_floor), .gt(comparator_5_gt));  // open: eq, lt
  Subtractor #(.width(4)) subtractor_1 (.a(req_floor), .b(lift_1_md), .out(subtractor_1_out));  // open: bin, bout
  Subtractor #(.width(4)) subtractor_2 (.a(lift_1_md), .b(req_floor), .out(subtractor_2_out));  // open: bin, bout
  Comparator #(.width(4)) comparator_6 (.a(lift_2_md), .b(req_floor), .gt(comparator_6_gt));  // open: eq, lt
  Subtractor #(.width(4)) subtractor_3 (.a(req_floor), .b(lift_2_md), .out(subtractor_3_out));  // open: bin, bout
  Subtractor #(.width(4)) subtractor_4 (.a(lift_2_md), .b(req_floor), .out(subtractor_4_out));  // open: bin, bout
  xnor xnor_1 (xnor_1_out, comparator_1_gt, comparator_2_gt);
  Multiplexer #(.width(2), .enable("false")) multiplexer_1 (
    .in0(2'b01), .in1(2'b10), .out(multiplexer_1_out), .sel(xnor_1_out));
  xnor xnor_2 (xnor_2_out, comparator_3_gt, comparator_4_gt);
  Multiplexer #(.width(2), .enable("false")) multiplexer_2 (
    .in0(2'b10), .in1(2'b01), .out(multiplexer_2_out), .sel(xnor_2_out));
  Multiplexer #(.width(4), .enable("false")) multiplexer_3 (
    .in0(subtractor_1_out), .in1(subtractor_2_out), .out(multiplexer_3_out), .sel(comparator_5_gt));
  Multiplexer #(.width(4), .enable("false")) multiplexer_4 (
    .in0(subtractor_3_out), .in1(subtractor_4_out), .out(multiplexer_4_out), .sel(comparator_6_gt));
  Comparator #(.width(4)) comparator_7 (
    .a(multiplexer_3_out), .b(multiplexer_4_out), .gt(comparator_7_gt));  // open: eq, lt
  and and_1 (and_1_out, lift_1_im, lift_2_im);
  Multiplexer #(.width(2), .enable("false")) multiplexer_5 (
    .in0(multiplexer_1_out), .in1(multiplexer_2_out), .out(multiplexer_5_out), .sel(lift_2_im));
  Multiplexer #(.width(2), .enable("false")) multiplexer_6 (
    .in0(2'b01), .in1(2'b10), .out(multiplexer_6_out), .sel(comparator_7_gt));
  Multiplexer #(.width(2), .enable("false")) multiplexer_7 (
    .in0(multiplexer_6_out), .in1(2'b10), .out(multiplexer_7_out), .sel(xnor_1_out));
  Multiplexer #(.width(2), .enable("false")) multiplexer_8 (
    .in0(multiplexer_7_out), .in1(2'b01), .out(multiplexer_8_out), .sel(xnor_2_out));
  Multiplexer #(.width(2), .enable("false")) multiplexer_9 (
    .in0(multiplexer_5_out), .in1(multiplexer_8_out), .out(chosen_lift), .sel(and_1_out));
endmodule

module lift_controller (
  input  [3:0] req_floor,
  input  selector,
  input  clock,
  input  Reset,
  output lift_im,
  output [3:0] lift_floor,
  output [3:0] lift_md
);

  wire and_1_out, comparator_1_eq, comparator_1_gt, comparator_2_eq, comparator_2_gt, comparator_2_lt,
       not_1_out, or_1_out, or_2_out, or_3_out, xnor_1_out;

  or or_1 (or_1_out, not_1_out, selector);
  Register #(.width(1), .trigger("falling")) is_moving_1 (
    .D(or_1_out), .Q(lift_im), .clk(clock), .clr(Reset));  // open: en
  and and_1 (and_1_out, xnor_1_out, selector);
  Register #(.width(4)) max_d_1 (.D(req_floor), .Q(lift_md), .clk(and_1_out), .clr(Reset));  // open: en
  Counter #(.width(4), .max('hf)) floor_1 (
    .load(comparator_2_lt), .D(lift_floor), .count(lift_im), .Q(lift_floor), .clk(clock), .clr(Reset));  // open: carry
  not not_1 (not_1_out, comparator_2_eq);
  Comparator #(.width(4)) comparator_1 (
    .a(req_floor), .b(lift_md), .gt(comparator_1_gt), .eq(comparator_1_eq));  // open: lt
  Comparator #(.width(4)) comparator_2 (
    .a(lift_md), .b(lift_floor), .gt(comparator_2_gt), .eq(comparator_2_eq), .lt(comparator_2_lt));
  or or_2 (or_2_out, comparator_1_gt, comparator_1_eq);
  or or_3 (or_3_out, comparator_2_gt, comparator_2_eq);
  xnor xnor_1 (xnor_1_out, or_2_out, or_3_out);
endmodule
